# Fritzing sketch toggleLED (saved by Fritzing 0.9.2b)
breadboards: 1

parts:
  Raspberry_Pi_2 = Raspberry Pi 2
  R1 = Resistor [tolerance=±5% resistance=330 package=THT]
  LED1 = LED - 5mm [color="Red (633nm)" package="5 mm [THT]"]
  LED2 = LED - 5mm [color="Yellow (592nm)" package="5 mm [THT]"]
  Push_Button_Switch = Pushbutton [package="[THT]"]
  Capacitor = Ceramic Capacitor [capacitance=100nF package="100 mil [THT, multilayer]"]

nets:
  3V3: Raspberry_Pi_2.3v3, Raspberry_Pi_2.3V3, LED2.anode
  N1: Raspberry_Pi_2.GND, LED1.cathode, Push_Button_Switch.Pin_1, Push_Button_Switch.Pin_2, Capacitor.1
  N2: Raspberry_Pi_2.GPIO17, R1.Pin_0
  N3: Raspberry_Pi_2.GPIO18, Push_Button_Switch.Pin_3, Push_Button_Switch.Pin_4, Capacitor.0
  N4: R1.Pin_1, LED1.anode, LED2.cathode
